# Fritzing sketch ModuloEnergia (saved by Fritzing 0.9.5d)
circuit board: 8.49881cm x 4.6053cm

parts:
  Casc = Screw terminal - 2 pins [package=THT]
  Irrig = Screw terminal - 2 pins [package=THT]
  Lamp = Screw terminal - 2 pins [package=THT]
  Bomba = Screw terminal - 2 pins [package=THT]
  Umifi = Screw terminal - 2 pins [package=THT]
  Casc1 = Screw terminal - 2 pins [package=THT]
  Umifi1 = Screw terminal - 2 pins [package=THT]
  Bomba1 = Screw terminal - 2 pins [package=THT]
  Lamp1 = Screw terminal - 2 pins [package=THT]
  Irrig1 = Screw terminal - 2 pins [package=THT]
  Entrada = screw terminal, 6 pins

nets:
  N1: Casc.pin1, Irrig.pin1, Lamp.pin1, Bomba.pin1, Umifi.pin1, Entrada.pin1, Entrada.pin2, Entrada.pin3
  N2: Casc.pin2, Casc1.pin1
  N3: Irrig.pin2, Irrig1.pin1
  N4: Lamp.pin2, Lamp1.pin1
  N5: Bomba.pin2, Bomba1.pin1
  N6: Umifi.pin2, Umifi1.pin1
  N7: Casc1.pin2, Umifi1.pin2, Bomba1.pin2, Lamp1.pin2, Irrig1.pin2, Entrada.pin4, Entrada.pin5, Entrada.pin6
