# Fritzing sketch ModuloPrincipal (saved by Fritzing 0.9.5d)
circuit board: 14.2322cm x 10.4607cm

parts:
  Nano = Arduino Nano (Rev3.0)
  Relógio = ZS-042 RTC Module
  Trêm = female pin header, 3 pins [form="♀ (female)"]
  Controlador_de_Relê = female pin header, 10 pins [form="♀ (female)"]
  5v = female pin header, 2 pins [form="♀ (female)"]
  Boia = female pin header, 2 pins [form="♀ (female)"]
  Nível = female pin header, 3 pins [form="♀ (female)"]

nets (from the pcb view):
  GND: Nano.GND, Relógio.GND, Controlador_de_Relê.pin10, 5v.pin2, Boia.pin2, Nível.pin3
  N1: Nano.D2, Controlador_de_Relê.pin9
  N2: Nano.D3, Controlador_de_Relê.pin8
  N3: Nano.D4, Controlador_de_Relê.pin7
  N4: Nano.D5, Controlador_de_Relê.pin6
  N5: Nano.D6, Controlador_de_Relê.pin5
  N6: Nano.D7, Controlador_de_Relê.pin4
  N7: Nano.D8, Controlador_de_Relê.pin3
  N8: Nano.D9, Controlador_de_Relê.pin2
  N9: Nano.D10, Trêm.pin3
  N10: Nano.D11/MOSI, Trêm.pin2
  N11: Nano.D12/MISO, Trêm.pin1
  N12: Nano.VIN, 5v.pin1
  5V: Nano.5V, Relógio.VCC, Controlador_de_Relê.pin1, Nível.pin2
  N13: Nano.A7, Nível.pin1
  N14: Nano.A6, Boia.pin1
  N15: Nano.A5, Relógio.SCL
  N16: Nano.A4, Relógio.SDA

notes:
  Tela
